// Digital circuit first.dig as structural Verilog
module first (
  input  x_0,
  output a_0
);

  wire nand_1_out, nand_2_out, not_1_out, not_2_out, or_1_out;

  nand nand_1 (nand_1_out, x_0, x_0);
  not not_1 (not_1_out, x_0);
  not not_2 (not_2_out, nand_1_out);
  nand nand_2 (nand_2_out, nand_1_out, x_0);
  or or_1 (or_1_out, not_1_out, not_2_out);
  nand nand_3 (a_0, or_1_out, nand_2_out);
endmodule
