// Digital circuit last.dig as structural Verilog
module last (
  input  x_39,
  output a_39
);

  wire nand_1_out, nand_2_out, not_1_out, not_2_out, or_1_out;

  nand nand_1 (nand_1_out, x_39, x_39);
  not not_1 (not_1_out, x_39);
  not not_2 (not_2_out, nand_1_out);
  nand nand_2 (nand_2_out, nand_1_out, x_39);
  or or_1 (or_1_out, not_1_out, not_2_out);
  and and_1 (a_39, or_1_out, nand_2_out);
endmodule
