// Digital circuit quarantaine.dig as structural Verilog
module quarantaine (
  input  x_0,
  input  x_1,
  input  x_2,
  input  x_3,
  input  x_4,
  input  x_5,
  input  x_6,
  input  x_7,
  input  x_8,
  input  x_9,
  input  x_10,
  input  x_11,
  input  x_12,
  input  x_13,
  input  x_14,
  input  x_15,
  input  x_16,
  input  x_17,
  input  x_18,
  input  x_19,
  input  x_20,
  input  x_21,
  input  x_22,
  input  x_23,
  input  x_24,
  input  x_25,
  input  x_26,
  input  x_27,
  input  x_28,
  input  x_29,
  input  x_30,
  input  x_31,
  input  x_32,
  input  x_33,
  input  x_34,
  input  x_35,
  input  x_36,
  input  x_37,
  input  x_38,
  input  x_39,
  output y_0,
  output y_2,
  output y_1,
  output y_4,
  output y_3,
  output y_6,
  output y_5,
  output y_8,
  output y_7,
  output y_10,
  output y_9,
  output y_12,
  output y_11,
  output y_14,
  output y_13,
  output y_16,
  output y_15,
  output y_18,
  output y_17,
  output y_20,
  output y_19,
  output y_22,
  output y_21,
  output y_24,
  output y_23,
  output y_26,
  output y_25,
  output y_28,
  output y_27,
  output y_30,
  output y_29,
  output y_32,
  output y_31,
  output y_34,
  output y_33,
  output y_36,
  output y_35,
  output y_38,
  output y_37,
  output y_39
);

  wire first_1_a_0, last_1_a_39, nand_1_out, nand_2_out, not_1_out, not_2_out, not_3_out, not_4_out,
       not_5_out, not_6_out, not_7_out, not_8_out, not_9_out, not_10_out, not_11_out, not_12_out, not_13_out,
       not_14_out, not_15_out, not_16_out, not_17_out, swap_1_a_n, swap_1_a_n_plus_1, swap_2_a_n,
       swap_2_a_n_plus_1, swap_3_a_n, swap_3_a_n_plus_1, swap_4_a_n, swap_4_a_n_plus_1, swap_5_a_n,
       swap_5_a_n_plus_1, swap_6_a_n, swap_6_a_n_plus_1, swap_7_a_n, swap_7_a_n_plus_1, swap_8_a_n,
       swap_8_a_n_plus_1, swap_9_a_n, swap_9_a_n_plus_1, swap_10_a_n, swap_10_a_n_plus_1, swap_11_a_n,
       swap_11_a_n_plus_1, swap_12_a_n, swap_12_a_n_plus_1, swap_13_a_n, swap_13_a_n_plus_1, swap_14_a_n,
       swap_14_a_n_plus_1, swap_15_a_n, swap_15_a_n_plus_1, swap_16_a_n, swap_16_a_n_plus_1, swap_17_a_n,
       swap_17_a_n_plus_1, swap_18_a_n, swap_18_a_n_plus_1, swap_19_a_n, swap_19_a_n_plus_1;

  first first_1 (.x_0(x_0), .a_0(first_1_a_0));
  swap swap_1 (.x_n(x_1), .x_n_plus_1(x_2), .a_n(swap_1_a_n), .a_n_plus_1(swap_1_a_n_plus_1));
  swap swap_2 (.x_n(x_3), .x_n_plus_1(x_4), .a_n(swap_2_a_n), .a_n_plus_1(swap_2_a_n_plus_1));
  swap swap_3 (.x_n(x_5), .x_n_plus_1(x_6), .a_n(swap_3_a_n), .a_n_plus_1(swap_3_a_n_plus_1));
  swap swap_4 (.x_n(x_7), .x_n_plus_1(x_8), .a_n(swap_4_a_n), .a_n_plus_1(swap_4_a_n_plus_1));
  swap swap_5 (.x_n(x_9), .x_n_plus_1(x_10), .a_n(swap_5_a_n), .a_n_plus_1(swap_5_a_n_plus_1));
  swap swap_6 (.x_n(x_11), .x_n_plus_1(x_12), .a_n(swap_6_a_n), .a_n_plus_1(swap_6_a_n_plus_1));
  swap swap_7 (.x_n(x_13), .x_n_plus_1(x_14), .a_n(swap_7_a_n), .a_n_plus_1(swap_7_a_n_plus_1));
  swap swap_8 (.x_n(x_15), .x_n_plus_1(x_16), .a_n(swap_8_a_n), .a_n_plus_1(swap_8_a_n_plus_1));
  swap swap_9 (.x_n(x_17), .x_n_plus_1(x_18), .a_n(swap_9_a_n), .a_n_plus_1(swap_9_a_n_plus_1));
  swap swap_10 (.x_n(x_19), .x_n_plus_1(x_20), .a_n(swap_10_a_n), .a_n_plus_1(swap_10_a_n_plus_1));
  swap swap_11 (.x_n(x_21), .x_n_plus_1(x_22), .a_n(swap_11_a_n), .a_n_plus_1(swap_11_a_n_plus_1));
  swap swap_12 (.x_n(x_23), .x_n_plus_1(x_24), .a_n(swap_12_a_n), .a_n_plus_1(swap_12_a_n_plus_1));
  swap swap_13 (.x_n(x_25), .x_n_plus_1(x_26), .a_n(swap_13_a_n), .a_n_plus_1(swap_13_a_n_plus_1));
  swap swap_14 (.x_n(x_27), .x_n_plus_1(x_28), .a_n(swap_14_a_n), .a_n_plus_1(swap_14_a_n_plus_1));
  swap swap_15 (.x_n(x_29), .x_n_plus_1(x_30), .a_n(swap_15_a_n), .a_n_plus_1(swap_15_a_n_plus_1));
  swap swap_16 (.x_n(x_31), .x_n_plus_1(x_32), .a_n(swap_16_a_n), .a_n_plus_1(swap_16_a_n_plus_1));
  swap swap_17 (.x_n(x_33), .x_n_plus_1(x_34), .a_n(swap_17_a_n), .a_n_plus_1(swap_17_a_n_plus_1));
  swap swap_18 (.x_n(x_35), .x_n_plus_1(x_36), .a_n(swap_18_a_n), .a_n_plus_1(swap_18_a_n_plus_1));
  swap swap_19 (.x_n(x_37), .x_n_plus_1(x_38), .a_n(swap_19_a_n), .a_n_plus_1(swap_19_a_n_plus_1));
  last last_1 (.x_39(x_39), .a_39(last_1_a_39));
  not not_1 (not_1_out, first_1_a_0);
  not not_2 (not_2_out, not_1_out);
  not not_3 (not_3_out, not_2_out);
  not not_4 (not_4_out, not_3_out);
  not not_5 (not_5_out, not_6_out);
  not not_6 (not_6_out, not_7_out);
  not not_7 (not_7_out, not_8_out);
  not not_8 (not_8_out, last_1_a_39);
  nand nand_1 (nand_1_out, first_1_a_0, first_1_a_0);
  nand nand_2 (nand_2_out, last_1_a_39, last_1_a_39);
  not not_9 (not_9_out, nand_1_out);
  not not_10 (not_10_out, not_9_out);
  not not_11 (not_11_out, not_10_out);
  not not_12 (not_12_out, not_11_out);
  not not_13 (not_13_out, not_14_out);
  not not_14 (not_14_out, not_15_out);
  not not_15 (not_15_out, nand_2_out);
  not not_16 (not_16_out, nand_1_out);
  not not_17 (not_17_out, nand_2_out);
  \xor  xor_1 (.c(x_0), .d(not_16_out), .y(y_0));
  \xor  xor_2 (.c(first_1_a_0), .d(swap_1_a_n), .y(y_1));
  \xor  xor_3 (.c(not_9_out), .d(swap_1_a_n_plus_1), .y(y_2));
  \xor  xor_4 (.c(first_1_a_0), .d(swap_2_a_n), .y(y_3));
  \xor  xor_5 (.c(not_9_out), .d(swap_2_a_n_plus_1), .y(y_4));
  \xor  xor_6 (.c(not_1_out), .d(swap_3_a_n), .y(y_5));
  \xor  xor_7 (.c(not_10_out), .d(swap_3_a_n_plus_1), .y(y_6));
  \xor  xor_8 (.c(not_1_out), .d(swap_4_a_n), .y(y_7));
  \xor  xor_9 (.c(not_10_out), .d(swap_4_a_n_plus_1), .y(y_8));
  \xor  xor_10 (.c(not_1_out), .d(swap_5_a_n), .y(y_9));
  \xor  xor_11 (.c(not_10_out), .d(swap_5_a_n_plus_1), .y(y_10));
  \xor  xor_12 (.c(not_2_out), .d(swap_6_a_n), .y(y_11));
  \xor  xor_13 (.c(not_10_out), .d(swap_6_a_n_plus_1), .y(y_12));
  \xor  xor_14 (.c(not_3_out), .d(swap_7_a_n), .y(y_13));
  \xor  xor_15 (.c(not_11_out), .d(swap_7_a_n_plus_1), .y(y_14));
  \xor  xor_16 (.c(not_3_out), .d(swap_8_a_n), .y(y_15));
  \xor  xor_17 (.c(not_11_out), .d(swap_8_a_n_plus_1), .y(y_16));
  \xor  xor_18 (.c(not_3_out), .d(swap_9_a_n), .y(y_17));
  \xor  xor_19 (.c(not_11_out), .d(swap_9_a_n_plus_1), .y(y_18));
  \xor  xor_20 (.c(not_3_out), .d(swap_10_a_n), .y(y_19));
  \xor  xor_21 (.c(not_11_out), .d(swap_10_a_n_plus_1), .y(y_20));
  \xor  xor_22 (.c(not_4_out), .d(swap_11_a_n), .y(y_21));
  \xor  xor_23 (.c(not_12_out), .d(swap_11_a_n_plus_1), .y(y_22));
  \xor  xor_24 (.c(not_4_out), .d(swap_12_a_n), .y(y_23));
  \xor  xor_25 (.c(not_13_out), .d(swap_12_a_n_plus_1), .y(y_24));
  \xor  xor_26 (.c(not_5_out), .d(swap_13_a_n), .y(y_25));
  \xor  xor_27 (.c(not_14_out), .d(swap_13_a_n_plus_1), .y(y_26));
  \xor  xor_28 (.c(not_5_out), .d(swap_14_a_n), .y(y_27));
  \xor  xor_29 (.c(not_15_out), .d(swap_14_a_n_plus_1), .y(y_28));
  \xor  xor_30 (.c(not_5_out), .d(swap_15_a_n), .y(y_29));
  \xor  xor_31 (.c(not_15_out), .d(swap_15_a_n_plus_1), .y(y_30));
  \xor  xor_32 (.c(not_6_out), .d(swap_16_a_n), .y(y_31));
  \xor  xor_33 (.c(not_15_out), .d(swap_16_a_n_plus_1), .y(y_32));
  \xor  xor_34 (.c(not_7_out), .d(swap_17_a_n), .y(y_33));
  \xor  xor_35 (.c(not_15_out), .d(swap_17_a_n_plus_1), .y(y_34));
  \xor  xor_36 (.c(not_8_out), .d(swap_18_a_n), .y(y_35));
  \xor  xor_37 (.c(nand_2_out), .d(swap_18_a_n_plus_1), .y(y_36));
  \xor  xor_38 (.c(not_8_out), .d(swap_19_a_n), .y(y_37));
  \xor  xor_39 (.c(nand_2_out), .d(swap_19_a_n_plus_1), .y(y_38));
  \xor  xor_40 (.c(not_17_out), .d(x_39), .y(y_39));
endmodule
