// Digital circuit swap.dig as structural Verilog
module swap (
  input  x_n,
  input  x_n_plus_1,
  output a_n,
  output a_n_plus_1
);

  wire nand_1_out, nand_2_out, nand_3_out, nand_4_out, nand_5_out, nand_6_out, xor_1_out;

  xor xor_1 (xor_1_out, x_n, x_n_plus_1);
  nand nand_1 (nand_1_out, x_n, xor_1_out);
  nand nand_2 (nand_2_out, xor_1_out, x_n_plus_1);
  nand nand_3 (nand_3_out, x_n, nand_1_out);
  nand nand_4 (nand_4_out, nand_1_out, xor_1_out);
  nand nand_5 (nand_5_out, xor_1_out, nand_2_out);
  nand nand_6 (nand_6_out, nand_2_out, x_n_plus_1);
  nand nand_7 (a_n, nand_3_out, nand_4_out);
  nand nand_8 (a_n_plus_1, nand_5_out, nand_6_out);
endmodule
