// Digital circuit xor.dig as structural Verilog
module \xor  (
  input  c,
  input  d,
  output y
);

  wire nand_1_out, nand_2_out, not_1_out, not_2_out, or_1_out;

  nand nand_1 (nand_1_out, c, d);
  not not_1 (not_1_out, c);
  not not_2 (not_2_out, nand_1_out);
  or or_1 (or_1_out, not_1_out, not_2_out);
  nand nand_2 (nand_2_out, nand_1_out, d);
  nand nand_3 (y, or_1_out, nand_2_out);
endmodule
